// Logisim project CPU.circ as structural Verilog: 5 circuits, main circuit Alu
module main (
  input  [19:0] in_1,
  input  [19:0] in_2,
  input  [19:0] in_3,
  input  [19:0] in_4,
  input  in_5
);

  wire clock_1_out, control_unit_1_out_2, control_unit_1_out_3, control_unit_1_out_4, control_unit_1_out_5,
       control_unit_1_out_6, control_unit_1_out_7, undriven;
  wire [2:0] control_unit_1_aluop, undriven_3;
  wire [3:0] multiplexer_2_out;
  wire [7:0] rom_1_data;
  wire [19:0] adder_1_out, adder_2_out, bit_extender_1_out, bit_extender_2_out, multiplexer_3_out,
       ram_1_data, register_1_q, register_file_1_read_data2, undriven_2;
  wire [19:8] rom_1_data_2;

  Register #(.width(20)) register_1 (.D(in_1), .Q(register_1_q), .clk(clock_1_out), .clr(undriven));  // open: en
  Clock clock_1 (.out(clock_1_out));
  Bit_Extender #(.in_width(16), .out_width(20)) bit_extender_1 (.out(bit_extender_1_out));  // open: in
  Adder #(.width(20)) adder_1 (.a(undriven_2), .b(register_1_q), .out(adder_1_out));  // open: cin, cout
  assign bit_extender_2_out = {{12{rom_1_data[7]}}, rom_1_data};  // Bit_Extender bit_extender_2
  ROM #(.addrWidth(20), .dataWidth(20)) rom_1 (.addr(register_1_q), .data({rom_1_data_2, rom_1_data}));  // open: sel
  Multiplexer #(.width(20), .enable("false")) multiplexer_1 (
    .in0(adder_1_out), .in1(adder_2_out), .out(in_1));  // open: sel
  Adder #(.width(20)) adder_2 (.a(bit_extender_1_out), .b(adder_1_out), .out(adder_2_out));  // open: cin, cout
  Control_unit control_unit_1 (
    .OpCode(rom_1_data_2[19:16]), .out_2(control_unit_1_out_2), .out_3(control_unit_1_out_3),
    .out_4(control_unit_1_out_4), .out_5(control_unit_1_out_5), .out_6(control_unit_1_out_6),
    .out_7(control_unit_1_out_7), .ALUop(control_unit_1_aluop));
  Register_file register_file_1 (
    .write_data(in_4), .read_data1(in_3), .read_data2(register_file_1_read_data2),
    .write_register(rom_1_data_2[15:12]), .regWrite(undriven), .clock(control_unit_1_out_4),
    .read_reg1(rom_1_data_2[11:8]), .read_reg2(multiplexer_2_out));
  Multiplexer #(.width(4), .enable("false")) multiplexer_2 (
    .in0(rom_1_data_2[11:8]), .in1(rom_1_data[7:4]), .out(multiplexer_2_out), .sel(control_unit_1_out_2));
  Alu_control alu_control_1 (.\function (rom_1_data[3:0]), .ALUop(control_unit_1_aluop), .OpSelector(undriven_3));
  Multiplexer #(.width(20), .enable("false")) multiplexer_3 (
    .in0(in_3), .in1(bit_extender_2_out), .out(multiplexer_3_out), .sel(control_unit_1_out_3));
  Alu alu_1 (.A(register_file_1_read_data2), .B(multiplexer_3_out), .ALU_Output(in_2), .OpSelector(undriven_3));
  RAM #(.addrWidth(20), .dataWidth(20), .bus("separate")) ram_1 (
    .addr(in_2), .din(in_3), .data(ram_1_data), .str(control_unit_1_out_7), .clk(clock_1_out),
    .ld(control_unit_1_out_5));  // open: sel, clr
  Multiplexer #(.width(20), .enable("false")) multiplexer_4 (
    .in0(in_2), .in1(ram_1_data), .out(in_4), .sel(control_unit_1_out_6));

  // Notes on the sheet:
  //   in_3: pull=up
endmodule

// ALU
module Alu (
  input  [19:0] A,
  input  [19:0] B,
  input  [19:0] ALU_Output,
  input  [2:0] OpSelector
);

  wire [19:0] adder_1_out, and_1_out, divider_1_out, multiplier_1_out, negator_1_out, nor_1_out, or_1_out,
       subtractor_1_out, undriven;

  Adder #(.width(20)) adder_1 (.a(A), .b(B), .out(adder_1_out));  // open: cin, cout
  Subtractor #(.width(20)) subtractor_1 (.a(A), .b(B), .out(subtractor_1_out));  // open: bin, bout
  Multiplier #(.width(20)) multiplier_1 (.a(A), .b(B), .out(multiplier_1_out));  // open: cin, cout
  Divider #(.width(20)) divider_1 (.a(A), .b(B), .out(divider_1_out));  // open: upper, rem
  Negator #(.width(20)) negator_1 (.in(B), .out(negator_1_out));
  assign and_1_out = A & B;  // AND_Gate and_1, 20 bits wide
  assign or_1_out = A | B;  // OR_Gate or_1, 20 bits wide
  assign nor_1_out = ~(A | B);  // NOR_Gate nor_1, 20 bits wide
  Multiplexer #(.select(3), .width(20), .enable("false")) multiplexer_1 (
    .in0(undriven), .in1(adder_1_out), .in2(subtractor_1_out), .in3(multiplier_1_out), .in4(divider_1_out),
    .in5(negator_1_out), .in6(and_1_out), .in7(or_1_out), .out(ALU_Output), .sel(OpSelector));
endmodule

// ALU control
module Alu_control (
  input  [2:0] OpSelector,
  input  [3:0] \function ,
  input  [2:0] ALUop
);

  wire [2:0] multiplexer_2_out, multiplexer_3_out, multiplexer_4_out, undriven, undriven_2, undriven_3,
       undriven_4;

  Multiplexer #(.width(3), .enable("false")) multiplexer_1 (
    .in0(multiplexer_4_out), .in1(\function [3:1]), .out(OpSelector), .sel(ALUop[2]));
  Multiplexer #(.width(3), .enable("false")) multiplexer_2 (
    .in0(undriven), .in1(undriven_2), .out(multiplexer_2_out), .sel(ALUop[1]));
  Multiplexer #(.width(3), .enable("false")) multiplexer_3 (
    .in0(undriven_3), .in1(undriven_4), .out(multiplexer_3_out), .sel(ALUop[0]));
  Multiplexer #(.width(3), .enable("false")) multiplexer_4 (
    .in0(multiplexer_3_out), .in1(multiplexer_2_out), .out(multiplexer_4_out), .sel(ALUop[1]));

  // Notes on the sheet:
  //   0
  //   4
  //   0
  //   5
endmodule

// Register
module Register_file (
  input  [3:0] read_reg1,
  input  [3:0] write_register,
  input  [3:0] read_reg2,
  input  regWrite,
  input  clock,
  input  [19:0] write_data,
  output [19:0] read_data1,
  output [19:0] read_data2
);

  wire and_1_out, and_2_out, and_3_out, and_4_out, and_5_out, and_6_out, and_7_out, and_8_out, and_9_out,
       and_10_out, and_11_out, and_12_out, and_13_out, and_14_out, and_15_out, and_16_out, decoder_1_out0,
       decoder_1_out1, decoder_1_out2, decoder_1_out3, decoder_1_out4, decoder_1_out5, decoder_1_out6,
       decoder_1_out7, decoder_1_out8, decoder_1_out9, decoder_1_out10, decoder_1_out11, decoder_1_out12,
       decoder_1_out13, decoder_1_out14, decoder_1_out15;
  wire [19:0] register_1_q, register_2_q, register_3_q, register_4_q, register_5_q, register_6_q,
       register_7_q, register_8_q, register_9_q, register_10_q, register_11_q, register_12_q, register_13_q,
       register_14_q, register_15_q;

  Decoder #(.select(4)) decoder_1 (
    .out0(decoder_1_out0), .out1(decoder_1_out1), .out2(decoder_1_out2), .out3(decoder_1_out3),
    .out4(decoder_1_out4), .out5(decoder_1_out5), .out6(decoder_1_out6), .out7(decoder_1_out7),
    .out8(decoder_1_out8), .out9(decoder_1_out9), .out10(decoder_1_out10), .out11(decoder_1_out11),
    .out12(decoder_1_out12), .out13(decoder_1_out13), .out14(decoder_1_out14), .out15(decoder_1_out15),
    .sel(write_register));  // open: en
  and and_1 (and_1_out, decoder_1_out0, regWrite);
  and and_2 (and_2_out, decoder_1_out1, regWrite);
  and and_3 (and_3_out, decoder_1_out2, regWrite);
  and and_4 (and_4_out, decoder_1_out3, regWrite);
  and and_5 (and_5_out, decoder_1_out4, regWrite);
  and and_6 (and_6_out, decoder_1_out5, regWrite);
  and and_7 (and_7_out, decoder_1_out6, regWrite);
  and and_8 (and_8_out, decoder_1_out7, regWrite);
  Register #(.width(20)) register_1 (.D(write_data), .Q(register_1_q), .clk(clock), .clr(and_1_out));  // open: en
  Register #(.width(20)) register_2 (.D(write_data), .Q(register_2_q), .clk(clock), .clr(and_2_out));  // open: en
  Register #(.width(20)) register_3 (.D(write_data), .Q(register_3_q), .clk(clock), .clr(and_3_out));  // open: en
  Register #(.width(20)) register_4 (.D(write_data), .Q(register_4_q), .clk(clock), .clr(and_4_out));  // open: en
  Register #(.width(20)) register_5 (.D(write_data), .Q(register_5_q), .clk(clock), .clr(and_5_out));  // open: en
  Register #(.width(20)) register_6 (.D(write_data), .Q(register_6_q), .clk(clock), .clr(and_6_out));  // open: en
  Register #(.width(20)) register_7 (.D(write_data), .Q(register_7_q), .clr(and_7_out));  // open: en, clk
  Register #(.width(20)) register_8 (.D(write_data), .Q(register_8_q), .clk(clock), .clr(and_8_out));  // open: en
  and and_9 (and_9_out, decoder_1_out8, regWrite);
  and and_10 (and_10_out, decoder_1_out9, regWrite);
  and and_11 (and_11_out, decoder_1_out10, regWrite);
  and and_12 (and_12_out, decoder_1_out11, regWrite);
  and and_13 (and_13_out, decoder_1_out12, regWrite);
  and and_14 (and_14_out, decoder_1_out13, regWrite);
  and and_15 (and_15_out, decoder_1_out14, regWrite);
  and and_16 (and_16_out, decoder_1_out15, regWrite);
  Register #(.width(20)) register_9 (.D(write_data), .Q(register_9_q), .clk(clock), .clr(and_9_out));  // open: en
  Register #(.width(20)) register_10 (.D(write_data), .Q(register_10_q), .clk(clock), .clr(and_10_out));  // open: en
  Register #(.width(20)) register_11 (.D(write_data), .Q(register_11_q), .clk(clock), .clr(and_11_out));  // open: en
  Register #(.width(20)) register_12 (.D(write_data), .Q(register_12_q), .clk(clock), .clr(and_12_out));  // open: en
  Register #(.width(20)) register_13 (.D(write_data), .Q(register_13_q), .clk(clock), .clr(and_13_out));  // open: en
  Register #(.width(20)) register_14 (.D(write_data), .Q(register_14_q), .clk(clock), .clr(and_14_out));  // open: en
  Register #(.width(20)) register_15 (.D(write_data), .Q(register_15_q), .clk(clock), .clr(and_15_out));  // open: en
  Register #(.width(20)) register_16 (.D(write_data), .Q(register_15_q), .clk(clock), .clr(and_16_out));  // open: en
  Multiplexer #(.select(4), .width(20)) multiplexer_1 (
    .in0(register_1_q), .in1(register_2_q), .in2(register_3_q), .in3(register_4_q), .in4(register_5_q),
    .in5(register_6_q), .in6(register_7_q), .in7(register_8_q), .in8(register_9_q), .in9(register_10_q),
    .in10(register_11_q), .in11(register_12_q), .in12(register_13_q), .in13(register_14_q),
    .in14(register_15_q), .in15(register_15_q), .out(read_data1), .sel(read_reg1));  // open: en
  Multiplexer #(.select(4), .width(20)) multiplexer_2 (
    .in0(register_1_q), .in1(register_2_q), .in2(register_3_q), .in3(register_4_q), .in4(register_5_q),
    .in5(register_6_q), .in6(register_7_q), .in7(register_8_q), .in8(register_9_q), .in9(register_10_q),
    .in10(register_11_q), .in11(register_12_q), .in12(register_13_q), .in13(register_14_q),
    .in14(register_15_q), .in15(register_15_q), .out(read_data2), .sel(read_reg2));  // open: en
endmodule

// Control unite
module Control_unit (
  input  [3:0] OpCode,
  output out_2,
  output out_3,
  output out_4,
  output out_5,
  output out_6,
  output out_7,
  output [2:0] ALUop
);

  and R_type (ALUop[1], ~OpCode[3], ~OpCode[2], ~OpCode[1], ~OpCode[0]);  // AND_Gate
  and lw (out_5, ~OpCode[3], ~OpCode[2], OpCode[1], OpCode[0]);  // AND_Gate
  and sw (out_7, OpCode[3], ~OpCode[2], OpCode[1], OpCode[0]);  // AND_Gate
  or or_1 (ALUop[0], out_7, out_5);
  or or_2 (out_3, out_5, out_7);
  or or_3 (out_4, ALUop[1], out_5);

  assign out_2 = ALUop[1];
  assign out_6 = out_5;
endmodule
